# Fritzing sketch tempsensor (saved by Fritzing 0.9.2b)
circuit board: 2.72344cm x 6.13833cm
breadboards: 1

parts:
  Part1 = Arduino Pro Mini v13
  Transceiver1 = nRF24L01 [package=module]
  DS1 = DS18B20 1-Wire Temperature Sensor [part_number=DS18B20]
  R1 = Resistor [tolerance=±5% resistance=220 package=THT]

nets:
  VCC: Part1.VCC, Transceiver1.VCC, DS1.VDD, R1.Pin_0
  GND: Part1.GND, Transceiver1.GND, DS1.GND
  N1: Part1.D13/SCK, Transceiver1.SCK
  N2: Part1.D12/MISO, Transceiver1.MISO
  N3: Part1.D11_PWM/MOSI, Transceiver1.MOSI
  N4: Part1.D10_PWM/SS, Transceiver1.CSN
  N5: Part1.D9_PWM, Transceiver1.CE
  N6: Part1.D3_PWM, DS1.DQ, R1.Pin_1
  N7: Part1.D2, Transceiver1.IRQ

custom parts:
  nRF24L01: nRF24L01 module
